# Fritzing sketch Body-sensor +led (saved by Fritzing 0.9.3b)
breadboards: 1

parts:
  Composant1 = HC-SR501 Body Sensor Module
  Composant2 = Arduino Uno (Rev3)
  LED1 = LED - 5mm [color="Red (633nm)" package="5 mm [THT]"]
  R1 = Resistor [tolerance=±5% resistance=220 package=THT]

nets:
  N1: Composant1.OUT, Composant2.D7
  N2: Composant1.GND, R1.Pin_1
  N3: Composant2.D4, LED1.cathode
  N4: LED1.anode, R1.Pin_0

custom parts:
  HC-SR501 Body Sensor Module: Pyroelectric Infrared PIR Motion Sensor Detector Module

// code stored in the sketch: Untitled.ino
int BODYSENSOR = 7;
int LED = 4;

void setup(){
pinMode(BODYSENSOR,INPUT);
pinMode(LED,OUTPUT);
}

void loop(){
if(digitalRead(BODYSENSOR)==HIGH){
digitalWrite(LED,HIGH);
delay(300000);
}
else{
digitalWrite(LED,LOW);
}
}
